// Logisim project MIPS.circ as structural Verilog: 1 circuit, main circuit main
module main (
);

  wire alu_1_zero, and_1_out, button_1_out, CLK, controlunit_1_p1, controlunit_1_p4, controlunit_1_p5,
       controlunit_1_p6, controlunit_1_p7, controlunit_1_p8, controlunit_1_p9;
  wire [3:0] controlunit_1_p10;
  wire [4:0] multiplexer_3_out;
  wire [27:0] adder_1_out, bit_extender_2_out, shifter_1_out;
  wire [31:0] adder_2_out, alu_1_alu_result, bit_extender_1_out, data_mem_1_rd, instmem_1_out_2,
       multiplexer_1_out, multiplexer_2_out, multiplexer_4_out, multiplexer_5_out, PC_q, regfile32_1_rd1,
       regfile32_1_rd2, shifter_2_out;
  wire [31:28] adder_1_out_2;

  Clock clock_1 (.out(CLK));
  // Probe on {adder_1_out_2, adder_1_out}
  Multiplexer #(.width(32)) multiplexer_1 (
    .in0({adder_1_out_2, adder_1_out}), .in1(adder_2_out), .out(multiplexer_1_out), .sel(and_1_out));  // open: en
  // Probe on adder_2_out
  Multiplexer #(.width(32)) multiplexer_2 (
    .in0(multiplexer_1_out), .in1({adder_1_out_2, shifter_1_out}), .out(multiplexer_2_out),
    .sel(controlunit_1_p1));  // open: en
  Button button_1 (.out(button_1_out));
  Register #(.width(32)) PC (.D(multiplexer_2_out), .Q(PC_q), .clk(CLK), .clr(button_1_out));  // open: en
  InstMem instmem_1 (.A(PC_q), .out_2(instmem_1_out_2));
  Adder #(.width(32)) adder_1 (.a(PC_q), .b(32'h4), .out({adder_1_out_2, adder_1_out}));  // open: cin, cout
  // ControlUnit controlunit_1: pin names not known; wires that end beside it: controlunit_1_p1, instmem_1_out_2[31:26], instmem_1_out_2[5:0], controlunit_1_p4, controlunit_1_p5, controlunit_1_p6, controlunit_1_p7, controlunit_1_p8, controlunit_1_p9, controlunit_1_p10
  assign bit_extender_1_out = {{16{instmem_1_out_2[15]}}, instmem_1_out_2[15:0]};  // Bit_Extender bit_extender_1
  assign bit_extender_2_out = {{2{instmem_1_out_2[25]}}, instmem_1_out_2[25:0]};  // Bit_Extender bit_extender_2
  RegFile32 regfile32_1 (
    .AD1(instmem_1_out_2[25:21]), .AD2(instmem_1_out_2[20:16]), .CLK(CLK), .WE(controlunit_1_p9),
    .AD3(multiplexer_3_out), .WD3(multiplexer_5_out), .RD1(regfile32_1_rd1), .RD2(regfile32_1_rd2));
  Multiplexer #(.width(5)) multiplexer_3 (
    .in0(instmem_1_out_2[20:16]), .in1(instmem_1_out_2[15:11]), .out(multiplexer_3_out),
    .sel(controlunit_1_p8));  // open: en
  Shifter #(.width(28)) shifter_1 (.in(bit_extender_2_out), .\dist (5'b00010), .out(shifter_1_out));
  Multiplexer #(.width(32)) multiplexer_4 (
    .in0(regfile32_1_rd2), .in1(bit_extender_1_out), .out(multiplexer_4_out), .sel(controlunit_1_p7));  // open: en
  // Probe on bit_extender_1_out
  ALU alu_1 (
    .SrcA(regfile32_1_rd1), .SrcB(multiplexer_4_out), .ALU_Control(controlunit_1_p10), .Zero(alu_1_zero),
    .ALU_Result(alu_1_alu_result));
  // Probe on shifter_2_out
  // Probe on {adder_1_out_2, adder_1_out}
  Shifter #(.width(32)) shifter_2 (.in(bit_extender_1_out), .\dist (5'b00010), .out(shifter_2_out));
  and and_1 (and_1_out, controlunit_1_p6, alu_1_zero);
  Adder #(.width(32)) adder_2 (
    .a(shifter_2_out), .b({adder_1_out_2, adder_1_out}), .out(adder_2_out));  // open: cin, cout
  Data_Mem data_mem_1 (
    .A(alu_1_alu_result), .CLK(CLK), .WE(controlunit_1_p5), .WD(regfile32_1_rd2), .RD(data_mem_1_rd));
  Multiplexer #(.width(32)) multiplexer_5 (
    .in0(alu_1_alu_result), .in1(data_mem_1_rd), .out(multiplexer_5_out), .sel(controlunit_1_p4));  // open: en
endmodule
